# Fritzing sketch zmotion_arduino_schematic (saved by Fritzing 0.8.6b)
breadboards: 1
perfboards: 1

parts:
  Part1 = Arduino Uno (Rev3)
  R1 = Resistor [tolerance=±5% resistance=100k package=THT]
  R2 = Photocell (LDR) [package=THT]

nets:
  N1: Part1.3V3, R1.Pin_0
  N2: Part1.GND, R2.pin_1
  N3: R1.Pin_1, R2.pin_0

notes:
  Motion Detection Module (ZEPIR0AAS01SBCG)
  Pin 1
  Pin 8
  100K
  Photocell 100K
